// Logisim project adders.circ as structural Verilog: 2 circuits, main circuit one_bit_adder
// One Bit Adder
module one_bit_adder (
  input  A,
  input  B,
  input  C_in,
  output S,
  output C_out
);

  wire and_1_out, and_2_out, and_3_out, and_4_out, and_5_out, and_6_out, and_7_out, and_8_out, and_9_out,
       and_10_out, not_1_out, not_2_out, not_3_out, or_1_out, or_2_out, or_3_out;

  not not_1 (not_1_out, A);
  not not_2 (not_2_out, B);
  not not_3 (not_3_out, C_in);
  and and_1 (and_1_out, not_2_out, not_3_out);
  and and_2 (and_2_out, B, C_in);
  and and_3 (and_3_out, not_2_out, C_in);
  and and_4 (and_4_out, B, not_3_out);
  and and_5 (and_5_out, not_1_out, B);
  and and_6 (and_6_out, A, not_2_out);
  and and_7 (and_7_out, A, B);
  or or_1 (or_1_out, and_1_out, and_2_out);
  or or_2 (or_2_out, and_3_out, and_4_out);
  or or_3 (or_3_out, and_5_out, and_6_out);
  and and_8 (and_8_out, or_1_out, A);
  and and_9 (and_9_out, or_2_out, not_1_out);
  and and_10 (and_10_out, or_3_out, C_in);
  or or_4 (S, and_8_out, and_9_out);
  or or_5 (C_out, and_10_out, and_7_out);
endmodule

module two_bit_adder (
  input  [1:0] A,
  input  [1:0] B,
  input  in_3,
  output [1:0] S
);

  wire one_bit_adder_1_c_out;

  one_bit_adder one_bit_adder_1 (.A(A[0]), .B(B[0]), .C_in(in_3), .S(S[0]), .C_out(one_bit_adder_1_c_out));
  one_bit_adder one_bit_adder_2 (.A(A[1]), .B(B[1]), .C_in(one_bit_adder_1_c_out), .S(S[1]));  // open: C_out
endmodule
