// Logisim project nand_completeness.circ as structural Verilog: 6 circuits, main circuit nand_not
module nand_not (
  input  A,
  output NOT_A
);

  nand nand_1 (NOT_A, A, A);
endmodule

module nand_or (
  input  A,
  input  B,
  output A_OR_B
);

  wire nand_1_out, nand_2_out;

  nand nand_1 (nand_1_out, A, A);
  nand nand_2 (nand_2_out, B, B);
  nand nand_3 (A_OR_B, nand_1_out, nand_2_out);
endmodule

module nand_and (
  input  A,
  input  B,
  output A_AND_B
);

  wire nand_1_out;

  nand nand_1 (nand_1_out, A, B);
  nand nand_2 (A_AND_B, nand_1_out, nand_1_out);
endmodule

module nand_nor (
  input  A,
  input  B,
  output A_NOR_B
);

  wire nand_1_out, nand_2_out, nand_3_out;

  nand nand_1 (nand_1_out, A, A);
  nand nand_2 (nand_2_out, B, B);
  nand nand_3 (nand_3_out, nand_1_out, nand_2_out);
  nand nand_4 (A_NOR_B, nand_3_out, nand_3_out);
endmodule

module nand_xor (
  input  A,
  input  B,
  output A_XOR_B
);

  wire nand_1_out, nand_2_out, nand_3_out, nand_4_out, nand_5_out;

  nand nand_1 (nand_1_out, A, A);
  nand nand_2 (nand_2_out, A, B);
  nand nand_3 (nand_3_out, B, B);
  nand nand_4 (nand_4_out, nand_1_out, nand_3_out);
  nand nand_5 (nand_5_out, nand_2_out, nand_4_out);
  nand nand_6 (A_XOR_B, nand_5_out, nand_5_out);
endmodule

module nand_xnor (
  input  A,
  input  B,
  output A_XNOR_B
);

  wire nand_1_out, nand_2_out, nand_3_out, nand_4_out;

  nand nand_1 (nand_1_out, A, A);
  nand nand_2 (nand_2_out, A, B);
  nand nand_3 (nand_3_out, B, B);
  nand nand_4 (nand_4_out, nand_1_out, nand_3_out);
  nand nand_5 (A_XNOR_B, nand_2_out, nand_4_out);
endmodule
