// Logisim project nor_completeness.circ as structural Verilog: 6 circuits, main circuit nor_not
module nor_not (
  input  A,
  output NOT_A
);

  nor nor_1 (NOT_A, A, A);
endmodule

module nor_xor (
  input  A,
  input  B,
  output A_XOR_B
);

  wire nor_1_out, nor_2_out, nor_3_out, nor_5_out;

  nor nor_1 (nor_1_out, A, A);
  nor nor_2 (nor_2_out, A, B);
  nor nor_3 (nor_3_out, B, B);
  nor nor_4 (A_XOR_B, nor_2_out, nor_5_out);
  nor nor_5 (nor_5_out, nor_1_out, nor_3_out);
endmodule

module nor_or (
  input  A,
  input  B,
  output A_OR_B
);

  wire nor_1_out;

  nor nor_1 (nor_1_out, A, B);
  nor nor_2 (A_OR_B, nor_1_out, nor_1_out);
endmodule

module nor_and (
  input  A,
  input  B,
  output A_AND_B
);

  wire nor_1_out, nor_2_out;

  nor nor_1 (nor_1_out, A, A);
  nor nor_2 (nor_2_out, B, B);
  nor nor_3 (A_AND_B, nor_1_out, nor_2_out);
endmodule

module nor_nand (
  input  A,
  input  B,
  output A_NAND_B
);

  wire nor_1_out, nor_2_out, nor_3_out;

  nor nor_1 (nor_1_out, A, A);
  nor nor_2 (nor_2_out, nor_1_out, nor_3_out);
  nor nor_3 (nor_3_out, B, B);
  nor nor_4 (A_NAND_B, nor_2_out, nor_2_out);
endmodule

module nor_xnor (
  input  A,
  input  B,
  output A_XNOR_B
);

  wire nor_1_out, nor_2_out, nor_3_out, nor_4_out, nor_5_out;

  nor nor_1 (nor_1_out, A, A);
  nor nor_2 (nor_2_out, A, B);
  nor nor_3 (nor_3_out, B, B);
  nor nor_4 (nor_4_out, nor_2_out, nor_5_out);
  nor nor_5 (nor_5_out, nor_1_out, nor_3_out);
  nor nor_6 (A_XNOR_B, nor_4_out, nor_4_out);
endmodule
