// Logisim project decoders.circ as structural Verilog: 4 circuits, main circuit onetwo_decoder
module onetwo_decoder (
  input  C,
  output D0,
  output D1
);

  not not_1 (D0, C);

  assign D1 = C;
endmodule

module twofour_decoder (
  input  C0,
  input  C1,
  output D0,
  output D1,
  output D2,
  output D3
);

  wire not_1_out, not_2_out;

  not not_1 (not_1_out, C0);
  not not_2 (not_2_out, C1);
  and and_1 (D0, not_1_out, not_2_out);
  and and_2 (D1, not_1_out, C1);
  and and_3 (D2, C0, not_2_out);
  and and_4 (D3, C0, C1);
endmodule

module threeeight_decoder (
  input  C0,
  input  C1,
  input  C2,
  output D0,
  output D1,
  output D2,
  output D3,
  output D4,
  output D5,
  output D6,
  output D7
);

  wire not_1_out, not_2_out, not_3_out;

  not not_1 (not_1_out, C0);
  not not_2 (not_2_out, C1);
  not not_3 (not_3_out, C2);
  and and_1 (D0, not_1_out, not_2_out, not_3_out);
  and and_2 (D1, not_1_out, not_2_out, C2);
  and and_3 (D2, not_1_out, C1, not_3_out);
  and and_4 (D3, not_1_out, C1, C2);
  and and_5 (D4, C0, not_2_out, not_3_out);
  and and_6 (D5, C0, not_2_out, C2);
  and and_7 (D6, C0, C1, not_3_out);
  and and_8 (D7, C0, C1, C2);
endmodule

module foursixteen_decoder (
  input  C0,
  input  C1,
  input  C2,
  input  C3,
  output D0,
  output D1,
  output D2,
  output D3,
  output D4,
  output D5,
  output D6,
  output D7,
  output D8,
  output D9,
  output D10,
  output D11,
  output D12,
  output D13,
  output D14,
  output D15
);

  wire not_1_out, not_2_out, not_3_out, not_4_out;

  not not_1 (not_1_out, C0);
  not not_2 (not_2_out, C1);
  not not_3 (not_3_out, C2);
  not not_4 (not_4_out, C3);
  and and_1 (D0, not_1_out, not_2_out, not_3_out, not_4_out);
  and and_2 (D1, not_1_out, not_2_out, not_3_out, C3);
  and and_3 (D2, not_1_out, not_2_out, C2, not_4_out);
  and and_4 (D3, not_1_out, not_2_out, C2, C3);
  and and_5 (D4, not_1_out, C1, not_3_out, not_4_out);
  and and_6 (D5, not_1_out, C1, not_3_out, C3);
  and and_7 (D6, not_1_out, C1, C2, not_4_out);
  and and_8 (D7, not_1_out, C1, C2, C3);
  and and_9 (D8, C0, not_2_out, not_3_out, not_4_out);
  and and_10 (D9, C0, not_2_out, not_3_out, C3);
  and and_11 (D10, C0, not_2_out, C2, not_4_out);
  and and_12 (D11, C0, not_2_out, C2, C3);
  and and_13 (D12, C0, C1, not_3_out, not_4_out);
  and and_14 (D13, C0, C1, not_3_out, C3);
  and and_15 (D14, C0, C1, C2, not_4_out);
  and and_16 (D15, C0, C1, C2, C3);
endmodule
