// Logisim project encoders.circ as structural Verilog: 5 circuits, main circuit fourtwo_encoder_old
module fourtwo_encoder_old (
  input  D0,
  input  D1,
  input  D2,
  input  D3,
  output X0,
  output X1
);

  wire and_1_out, and_2_out, and_3_out, not_1_out, not_2_out, not_3_out, not_4_out;

  not not_1 (not_1_out, D0);
  not not_2 (not_2_out, D1);
  not not_3 (not_3_out, D2);
  not not_4 (not_4_out, D3);
  and and_1 (and_1_out, not_1_out, not_2_out, D2, not_4_out);
  and and_2 (and_2_out, not_1_out, not_2_out, not_3_out, D3);
  and and_3 (and_3_out, not_1_out, D1, not_3_out, not_4_out);
  or or_1 (X0, and_1_out, and_2_out);
  or or_2 (X1, and_2_out, and_3_out);
endmodule

module fourtwo_encoder (
  input  D0,
  input  D1,
  input  D2,
  input  D3,
  output X1,
  output X0
);

  or or_1 (X1, D1, D3);
  or or_2 (X0, D2, D3);
endmodule

module eightthree_encoder (
  input  D0,
  input  D1,
  input  D2,
  input  D3,
  input  D4,
  input  D5,
  input  D6,
  input  D7,
  output X0,
  output X1,
  output X2
);

  or or_1 (X0, D7, D6, D5, D4);
  or or_2 (X1, D7, D6, D3, D2);
  or or_3 (X2, D7, D5, D3, D1);
endmodule

module sixteenfour_encoder (
  input  D0,
  input  D1,
  input  D2,
  input  D3,
  input  D4,
  input  D5,
  input  D6,
  input  D7,
  input  D8,
  input  D9,
  input  D10,
  input  D11,
  input  D12,
  input  D13,
  input  D14,
  input  D15,
  output X0,
  output X1,
  output X2,
  output X3
);

  or or_1 (X0, D15, D14, D13, D12, D11, D10, D9, D8);
  or or_2 (X1, D15, D14, D13, D12, D7, D6, D5, D4);
  or or_3 (X2, D15, D14, D11, D10, D7, D6, D3, D2);
  or or_4 (X3, D15, D13, D11, D9, D7, D5, D3, D1);
endmodule

module eightthree_encoder_composite (
  input  D0,
  input  D1,
  input  D2,
  input  D3,
  input  D4,
  input  D5,
  input  D6,
  input  D7,
  output X0,
  output X2,
  output X1
);

  wire and_1_out, and_2_out, and_3_out, and_4_out, and_5_out, and_6_out, and_7_out, and_8_out, and_9_out,
       and_10_out, and_11_out, and_12_out, fourtwo_encoder_1_x0, fourtwo_encoder_1_x1, fourtwo_encoder_2_x0,
       fourtwo_encoder_2_x1, not_1_out, not_2_out, not_3_out, not_4_out, or_1_out, or_2_out, or_3_out,
       or_4_out, or_5_out;

  or or_1 (or_1_out, D0, D1, D2, D3);
  fourtwo_encoder fourtwo_encoder_1 (
    .D0(D0), .D1(D1), .D2(D2), .D3(D3), .X1(fourtwo_encoder_1_x1), .X0(fourtwo_encoder_1_x0));
  fourtwo_encoder fourtwo_encoder_2 (
    .D0(D4), .D1(D5), .D2(D6), .D3(D7), .X1(fourtwo_encoder_2_x1), .X0(fourtwo_encoder_2_x0));
  not not_1 (not_1_out, fourtwo_encoder_1_x1);
  not not_2 (not_2_out, fourtwo_encoder_1_x0);
  not not_3 (not_3_out, fourtwo_encoder_2_x1);
  not not_4 (not_4_out, fourtwo_encoder_2_x0);
  not not_5 (X0, or_1_out);
  and and_1 (and_1_out, fourtwo_encoder_1_x1, not_2_out);
  and and_2 (and_2_out, fourtwo_encoder_1_x1, fourtwo_encoder_1_x0);
  and and_3 (and_3_out, fourtwo_encoder_2_x1, not_4_out);
  and and_4 (and_4_out, fourtwo_encoder_2_x1, fourtwo_encoder_2_x0);
  and and_5 (and_5_out, not_1_out, fourtwo_encoder_1_x0);
  and and_6 (and_6_out, fourtwo_encoder_1_x1, fourtwo_encoder_1_x0);
  and and_7 (and_7_out, not_3_out, fourtwo_encoder_2_x0);
  and and_8 (and_8_out, fourtwo_encoder_2_x1, fourtwo_encoder_2_x0);
  or or_2 (or_2_out, and_1_out, and_2_out);
  or or_3 (or_3_out, and_3_out, and_4_out);
  or or_4 (or_4_out, and_5_out, and_6_out);
  or or_5 (or_5_out, and_7_out, and_8_out);
  and and_9 (and_9_out, or_2_out, or_1_out);
  and and_10 (and_10_out, or_3_out, X0);
  and and_11 (and_11_out, or_4_out, or_1_out);
  and and_12 (and_12_out, or_5_out, X0);
  or or_6 (X2, and_9_out, and_10_out);
  or or_7 (X1, and_11_out, and_12_out);
endmodule
