// Logisim project multiplexers.circ as structural Verilog: 4 circuits, main circuit twoone_multiplexer_old
module twoone_multiplexer_old (
  input  C0,
  input  D0,
  input  D1,
  output M
);

  wire and_1_out, and_2_out, and_3_out, not_1_out, not_2_out, not_3_out;

  not not_1 (not_1_out, C0);
  not not_2 (not_2_out, D0);
  not not_3 (not_3_out, D1);
  and and_1 (and_1_out, not_1_out, D0, not_3_out);
  and and_2 (and_2_out, C0, not_2_out, D1);
  or or_1 (M, and_1_out, and_2_out, and_3_out);
  and and_3 (and_3_out, D0, D1);
endmodule

module fourtwo_multiplexer (
  input  D0,
  input  D1,
  input  D2,
  input  D3,
  input  C0,
  input  C1,
  output M
);

  wire and_1_out, and_2_out, and_3_out, and_4_out, and_5_out, and_6_out, and_7_out, and_8_out, not_1_out,
       not_2_out;

  not not_1 (not_1_out, C0);
  not not_2 (not_2_out, C1);
  and and_1 (and_1_out, not_1_out, not_2_out);
  and and_2 (and_2_out, not_1_out, C1);
  and and_3 (and_3_out, C0, not_2_out);
  and and_4 (and_4_out, C0, C1);
  and and_5 (and_5_out, and_1_out, D0);
  and and_6 (and_6_out, and_2_out, D1);
  and and_7 (and_7_out, and_3_out, D2);
  and and_8 (and_8_out, and_4_out, D3);
  or or_1 (M, and_5_out, and_6_out, and_7_out, and_8_out);
endmodule

module twoone_multiplexer (
  input  D0,
  input  D1,
  input  C0,
  output M
);

  wire and_1_out, and_2_out, not_1_out;

  not not_1 (not_1_out, C0);
  and and_1 (and_1_out, not_1_out, D0);
  and and_2 (and_2_out, C0, D1);
  or or_1 (M, and_1_out, and_2_out);
endmodule

module eightthree_mutiplexer (
  input  in_1
);
endmodule
